# Fritzing sketch night_symphony-shield (saved by Fritzing 0.9.1b)
circuit board: 6.88566cm x 5.36311cm
breadboards: 1

parts:
  J1 = male pin header, 5 pins [form="♂ (male)"]
  J2 = male pin header, 5 pins [form="♂ (male)"]
  J3 = male pin header, 5 pins [form="♂ (male)"]
  J4 = male pin header, 5 pins [form="♂ (male)"]
  J5 = male pin header, 5 pins [form="♂ (male)"]
  J6 = male pin header, 5 pins [form="♂ (male)"]
  Q2 = TIP120 Hi-Current Darlington Transistor
  Q3 = TIP120 Hi-Current Darlington Transistor
  Q4 = TIP120 Hi-Current Darlington Transistor
  Q5 = TIP120 Hi-Current Darlington Transistor
  Q6 = TIP120 Hi-Current Darlington Transistor
  R1 = Resistor [tolerance=±5% resistance=220 package=THT]
  R2 = Resistor [tolerance=±5% resistance=220 package=THT]
  R4 = Resistor [tolerance=±5% resistance=220 package=THT]
  R5 = Resistor [tolerance=±5% resistance=220 package=THT]
  R6 = Resistor [tolerance=±5% resistance=220 package=THT]
  R3 = Resistor [tolerance=±5% resistance=220 package=THT]
  Q1 = TIP120 Hi-Current Darlington Transistor
  Part3 = Arduino Uno (Rev3)
  J7 = male pin header, 8 pins [form="♂ (male)"]
  LED1 = LED - 5mm [color="Red (633nm)" package="5 mm [THT]"]
  R7 = Resistor [tolerance=±5% resistance=220 package=THT]
  J8 = Power Jack [package=power_jack_pth]
  D1 = Diode [package=diode-1n4148]

nets:
  N1: J1.pin1, J2.pin1, J3.pin1, J4.pin1, J5.pin1, J6.pin1, J7.pin3, J8.PWR, D1.A
  N2: J1.pin2, Q1.COLLECTOR
  N3: J1.pin3, J2.pin3, J3.pin3, J4.pin3, J5.pin3, J6.pin3, Part3.5V, J7.pin1
  N4: J1.pin4, Part3.D8
  GND: J1.pin5, J2.pin5, J3.pin5, J4.pin5, J5.pin5, J6.pin5, Q2.EMITTER, Q3.EMITTER, Q4.EMITTER, Q5.EMITTER, Q6.EMITTER, Q1.EMITTER, Part3.GND, J7.pin2, LED1.cathode, J8.GND
  N5: J2.pin2, Q2.COLLECTOR
  N6: J2.pin4, Part3.D4
  N7: J3.pin2, Q3.COLLECTOR
  N8: J3.pin4, Part3.A5/SCL
  N9: J4.pin2, Q4.COLLECTOR
  N10: J4.pin4, Part3.D12/MISO
  N11: J5.pin2, Q5.COLLECTOR
  N12: J5.pin4, Part3.D7
  N13: J6.pin2, Q6.COLLECTOR
  N14: J6.pin4, Part3.D2
  N15: Q2.BASE, R2.Pin_0
  N16: Q3.BASE, R3.Pin_0
  N17: Q4.BASE, R4.Pin_0
  N18: Q5.BASE, R5.Pin_0
  N19: Q6.BASE, R6.Pin_0
  N20: R1.Pin_0, Q1.BASE
  N21: R1.Pin_1, Part3.D10_PWM/SS
  N22: R2.Pin_1, Part3.D6_PWM
  N23: R4.Pin_1, Part3.D11_PWM/MOSI
  N24: R5.Pin_1, Part3.D9_PWM
  N25: R6.Pin_1, Part3.D5_PWM
  N26: R3.Pin_1, Part3.D3_PWM
  N27: Part3.A0, J7.pin4
  N28: Part3.A1, J7.pin5
  N29: Part3.A2, J7.pin6
  N30: Part3.A3, J7.pin7
  N31: Part3.A4/SDA, J7.pin8
  N32: Part3.D13/SCK, R7.Pin_1
  N33: Part3.VIN, D1.C
  N34: LED1.anode, R7.Pin_0

notes:
  CMoP
  Night Symphony
  v0.1
